// Digital circuit 16bit_adder.dig as structural Verilog
module _16bit_adder (
  input  [15:0] A,
  input  [15:0] B,
  input  cin,
  output carry,
  output [15:0] sum
);

  wire _4bit_adder_1_carry, _4bit_adder_2_carry, _4bit_adder_3_carry;

  _4bit_adder _4bit_adder_1 (.A(A[3:0]), .B(B[3:0]), .cin(cin), .carry(_4bit_adder_1_carry), .sum(sum[3:0]));
  _4bit_adder _4bit_adder_2 (
    .A(A[7:4]), .B(B[7:4]), .cin(_4bit_adder_1_carry), .carry(_4bit_adder_2_carry), .sum(sum[7:4]));
  _4bit_adder _4bit_adder_3 (
    .A(A[11:8]), .B(B[11:8]), .cin(_4bit_adder_2_carry), .carry(_4bit_adder_3_carry), .sum(sum[11:8]));
  _4bit_adder _4bit_adder_4 (.A(A[15:12]), .B(B[15:12]), .cin(_4bit_adder_3_carry), .carry(carry), .sum(sum[15:12]));
endmodule
