// Digital circuit 16bit_register.dig as structural Verilog
module _16bit_register (
  input  [15:0] D,
  input  CLR,
  input  CLK,
  output [15:0] Q
);

  d_flipflop_clr d_flipflop_clr_1 (.D(D[0]), .CLR(CLR), .CLK(CLK), .Q(Q[0]));  // open: not_Q
  d_flipflop_clr d_flipflop_clr_2 (.D(D[1]), .CLR(CLR), .CLK(CLK), .Q(Q[1]));  // open: not_Q
  d_flipflop_clr d_flipflop_clr_3 (.D(D[2]), .CLR(CLR), .CLK(CLK), .Q(Q[2]));  // open: not_Q
  d_flipflop_clr d_flipflop_clr_4 (.D(D[3]), .CLR(CLR), .CLK(CLK), .Q(Q[3]));  // open: not_Q
  d_flipflop_clr d_flipflop_clr_5 (.D(D[4]), .CLR(CLR), .CLK(CLK), .Q(Q[4]));  // open: not_Q
  d_flipflop_clr d_flipflop_clr_6 (.D(D[5]), .CLR(CLR), .CLK(CLK), .Q(Q[5]));  // open: not_Q
  d_flipflop_clr d_flipflop_clr_7 (.D(D[6]), .CLR(CLR), .CLK(CLK), .Q(Q[6]));  // open: not_Q
  d_flipflop_clr d_flipflop_clr_8 (.D(D[7]), .CLR(CLR), .CLK(CLK), .Q(Q[7]));  // open: not_Q
  d_flipflop_clr d_flipflop_clr_9 (.D(D[8]), .CLR(CLR), .CLK(CLK), .Q(Q[8]));  // open: not_Q
  d_flipflop_clr d_flipflop_clr_10 (.D(D[9]), .CLR(CLR), .CLK(CLK), .Q(Q[9]));  // open: not_Q
  d_flipflop_clr d_flipflop_clr_11 (.D(D[10]), .CLR(CLR), .CLK(CLK), .Q(Q[10]));  // open: not_Q
  d_flipflop_clr d_flipflop_clr_12 (.D(D[11]), .CLR(CLR), .CLK(CLK), .Q(Q[11]));  // open: not_Q
  d_flipflop_clr d_flipflop_clr_13 (.D(D[12]), .CLR(CLR), .CLK(CLK), .Q(Q[12]));  // open: not_Q
  d_flipflop_clr d_flipflop_clr_14 (.D(D[13]), .CLR(CLR), .CLK(CLK), .Q(Q[13]));  // open: not_Q
  d_flipflop_clr d_flipflop_clr_15 (.D(D[14]), .CLR(CLR), .CLK(CLK), .Q(Q[14]));  // open: not_Q
  d_flipflop_clr d_flipflop_clr_16 (.D(D[15]), .CLR(CLR), .CLK(CLK), .Q(Q[15]));  // open: not_Q
endmodule
