// Digital circuit 2bit_multiplier.dig as structural Verilog
module _2bit_multiplier (
  input  [1:0] A,
  input  [1:0] B,
  output C_0,
  output C_2,
  output C_3,
  output C_4
);

  wire and_2_out, and_3_out, and_4_out, half_adder_1_carry;

  and and_1 (C_0, A[0], B[0]);
  and and_2 (and_2_out, A[1], B[0]);
  and and_3 (and_3_out, B[1], A[0]);
  and and_4 (and_4_out, A[1], B[1]);
  half_adder half_adder_1 (.A(and_2_out), .B(and_3_out), .Sum(C_2), .Carry(half_adder_1_carry));
  half_adder half_adder_2 (.A(half_adder_1_carry), .B(and_4_out), .Sum(C_3), .Carry(C_4));
endmodule
