// Digital circuit 2to1_1bit_mux.dig as structural Verilog
module _2to1_1bit_mux (
  input  S,
  input  A,
  input  B,
  output Out
);

  wire and_1_out, and_2_out;

  and and_1 (and_1_out, ~S, A);  // And
  and and_2 (and_2_out, S, B);
  or or_1 (Out, and_1_out, and_2_out);
endmodule
