// Digital circuit 32bit_2scomp.dig as structural Verilog
module _32bit_2scomp (
  input  [31:0] val,
  input  cin,
  output [31:0] NEG_val,
  output carry
);

  wire [31:0] not_1_out;

  not not_1 (not_1_out[0], val[0]);
  not not_2 (not_1_out[1], val[1]);
  not not_3 (not_1_out[2], val[2]);
  not not_4 (not_1_out[3], val[3]);
  not not_5 (not_1_out[4], val[4]);
  not not_6 (not_1_out[5], val[5]);
  not not_7 (not_1_out[6], val[6]);
  not not_8 (not_1_out[7], val[7]);
  not not_9 (not_1_out[8], val[8]);
  not not_10 (not_1_out[9], val[9]);
  not not_11 (not_1_out[10], val[10]);
  not not_12 (not_1_out[11], val[11]);
  not not_13 (not_1_out[12], val[12]);
  not not_14 (not_1_out[13], val[13]);
  not not_15 (not_1_out[14], val[14]);
  not not_16 (not_1_out[15], val[15]);
  not not_17 (not_1_out[16], val[16]);
  not not_18 (not_1_out[17], val[17]);
  not not_19 (not_1_out[18], val[18]);
  not not_20 (not_1_out[19], val[19]);
  not not_21 (not_1_out[20], val[20]);
  not not_22 (not_1_out[21], val[21]);
  not not_23 (not_1_out[22], val[22]);
  not not_24 (not_1_out[23], val[23]);
  not not_25 (not_1_out[24], val[24]);
  not not_26 (not_1_out[25], val[25]);
  not not_27 (not_1_out[26], val[26]);
  not not_28 (not_1_out[27], val[27]);
  not not_29 (not_1_out[28], val[28]);
  not not_30 (not_1_out[29], val[29]);
  not not_31 (not_1_out[30], val[30]);
  not not_32 (not_1_out[31], val[31]);
  _32bit_adder _32bit_adder_1 (.A(not_1_out), .B(32'h1), .cin(cin), .carry(carry), .sum(NEG_val));
endmodule
