// Digital circuit 32bit_adder.dig as structural Verilog
module _32bit_adder (
  input  [31:0] A,
  input  [31:0] B,
  input  cin,
  output carry,
  output [31:0] sum
);

  wire _16bit_adder_1_carry;

  _16bit_adder _16bit_adder_1 (.A(A[15:0]), .B(B[15:0]), .cin(cin), .carry(_16bit_adder_1_carry), .sum(sum[15:0]));
  _16bit_adder _16bit_adder_2 (.A(A[31:16]), .B(B[31:16]), .cin(_16bit_adder_1_carry), .carry(carry), .sum(sum[31:16]));

  // Notes on the sheet:
  //   A: default 4
  //   B: default 6
endmodule
