// Digital circuit 32bit_register_enable.dig as structural Verilog
module _32bit_register_enable (
  input  [31:0] D,
  input  CLR,
  input  CLK,
  output [31:0] Q
);

  d_flipflop_clr d_flipflop_clr_1 (.D(D[0]), .CLR(CLR), .CLK(CLK), .Q(Q[0]));  // open: not_Q
  d_flipflop_clr d_flipflop_clr_2 (.D(D[1]), .CLR(CLR), .CLK(CLK), .Q(Q[1]));  // open: not_Q
  d_flipflop_clr d_flipflop_clr_3 (.D(D[2]), .CLR(CLR), .CLK(CLK), .Q(Q[2]));  // open: not_Q
  d_flipflop_clr d_flipflop_clr_4 (.D(D[3]), .CLR(CLR), .CLK(CLK), .Q(Q[3]));  // open: not_Q
  d_flipflop_clr d_flipflop_clr_5 (.D(D[4]), .CLR(CLR), .CLK(CLK), .Q(Q[4]));  // open: not_Q
  d_flipflop_clr d_flipflop_clr_6 (.D(D[5]), .CLR(CLR), .CLK(CLK), .Q(Q[5]));  // open: not_Q
  d_flipflop_clr d_flipflop_clr_7 (.D(D[6]), .CLR(CLR), .CLK(CLK), .Q(Q[6]));  // open: not_Q
  d_flipflop_clr d_flipflop_clr_8 (.D(D[7]), .CLR(CLR), .CLK(CLK), .Q(Q[7]));  // open: not_Q
  d_flipflop_clr d_flipflop_clr_9 (.D(D[8]), .CLR(CLR), .CLK(CLK), .Q(Q[8]));  // open: not_Q
  d_flipflop_clr d_flipflop_clr_10 (.D(D[9]), .CLR(CLR), .CLK(CLK), .Q(Q[9]));  // open: not_Q
  d_flipflop_clr d_flipflop_clr_11 (.D(D[10]), .CLR(CLR), .CLK(CLK), .Q(Q[10]));  // open: not_Q
  d_flipflop_clr d_flipflop_clr_12 (.D(D[11]), .CLR(CLR), .CLK(CLK), .Q(Q[11]));  // open: not_Q
  d_flipflop_clr d_flipflop_clr_13 (.D(D[12]), .CLR(CLR), .CLK(CLK), .Q(Q[12]));  // open: not_Q
  d_flipflop_clr d_flipflop_clr_14 (.D(D[13]), .CLR(CLR), .CLK(CLK), .Q(Q[13]));  // open: not_Q
  d_flipflop_clr d_flipflop_clr_15 (.D(D[14]), .CLR(CLR), .CLK(CLK), .Q(Q[14]));  // open: not_Q
  d_flipflop_clr d_flipflop_clr_16 (.D(D[15]), .CLR(CLR), .CLK(CLK), .Q(Q[15]));  // open: not_Q
  d_flipflop_clr d_flipflop_clr_17 (.D(D[16]), .CLR(CLR), .CLK(CLK), .Q(Q[16]));  // open: not_Q
  d_flipflop_clr d_flipflop_clr_18 (.D(D[17]), .CLR(CLR), .CLK(CLK), .Q(Q[17]));  // open: not_Q
  d_flipflop_clr d_flipflop_clr_19 (.D(D[18]), .CLR(CLR), .CLK(CLK), .Q(Q[18]));  // open: not_Q
  d_flipflop_clr d_flipflop_clr_20 (.D(D[19]), .CLR(CLR), .CLK(CLK), .Q(Q[19]));  // open: not_Q
  d_flipflop_clr d_flipflop_clr_21 (.D(D[20]), .CLR(CLR), .CLK(CLK), .Q(Q[20]));  // open: not_Q
  d_flipflop_clr d_flipflop_clr_22 (.D(D[21]), .CLR(CLR), .CLK(CLK), .Q(Q[21]));  // open: not_Q
  d_flipflop_clr d_flipflop_clr_23 (.D(D[22]), .CLR(CLR), .CLK(CLK), .Q(Q[22]));  // open: not_Q
  d_flipflop_clr d_flipflop_clr_24 (.D(D[23]), .CLR(CLR), .CLK(CLK), .Q(Q[23]));  // open: not_Q
  d_flipflop_clr d_flipflop_clr_25 (.D(D[24]), .CLR(CLR), .CLK(CLK), .Q(Q[24]));  // open: not_Q
  d_flipflop_clr d_flipflop_clr_26 (.D(D[25]), .CLR(CLR), .CLK(CLK), .Q(Q[25]));  // open: not_Q
  d_flipflop_clr d_flipflop_clr_27 (.D(D[26]), .CLR(CLR), .CLK(CLK), .Q(Q[26]));  // open: not_Q
  d_flipflop_clr d_flipflop_clr_28 (.D(D[27]), .CLR(CLR), .CLK(CLK), .Q(Q[27]));  // open: not_Q
  d_flipflop_clr d_flipflop_clr_29 (.D(D[28]), .CLR(CLR), .CLK(CLK), .Q(Q[28]));  // open: not_Q
  d_flipflop_clr d_flipflop_clr_30 (.D(D[29]), .CLR(CLR), .CLK(CLK), .Q(Q[29]));  // open: not_Q
  d_flipflop_clr d_flipflop_clr_31 (.D(D[30]), .CLR(CLR), .CLK(CLK), .Q(Q[30]));  // open: not_Q
  d_flipflop_clr d_flipflop_clr_32 (.D(D[31]), .CLR(CLR), .CLK(CLK), .Q(Q[31]));  // open: not_Q
  // Pins of 16 and 32 bits meet at D
endmodule
