// Digital circuit 32bit_subber.dig as structural Verilog
module _32bit_subber (
  input  [31:0] POS_val,
  input  [31:0] NEG_val,
  output [31:0] difference,
  output carry
);

  wire [31:0] _32bit_2scomp_1_neg_val;

  _32bit_2scomp _32bit_2scomp_1 (.val(NEG_val), .cin(1'b0), .NEG_val(_32bit_2scomp_1_neg_val));  // open: carry
  _32bit_adder _32bit_adder_1 (.A(_32bit_2scomp_1_neg_val), .B(POS_val), .cin(1'b0), .carry(carry), .sum(difference));

  // Notes on the sheet:
  //   POS_val: default 10
  //   NEG_val: default 1
endmodule
