// Digital circuit 32bit_subber_2scomp.dig as structural Verilog
module _32bit_subber_2scomp (
  input  [31:0] in_1,
  output [31:0] out_2
);

  not not_1 (out_2[0], in_1[0]);
  not not_2 (out_2[1], in_1[1]);
  not not_3 (out_2[2], in_1[2]);
  not not_4 (out_2[3], in_1[3]);
  not not_5 (out_2[4], in_1[4]);
  not not_6 (out_2[5], in_1[5]);
  not not_7 (out_2[6], in_1[6]);
  not not_8 (out_2[7], in_1[7]);
  not not_9 (out_2[8], in_1[8]);
  not not_10 (out_2[9], in_1[9]);
  not not_11 (out_2[10], in_1[10]);
  not not_12 (out_2[11], in_1[11]);
  not not_13 (out_2[12], in_1[12]);
  not not_14 (out_2[13], in_1[13]);
  not not_15 (out_2[14], in_1[14]);
  not not_16 (out_2[15], in_1[15]);
  not not_17 (out_2[16], in_1[16]);
  not not_18 (out_2[17], in_1[17]);
  not not_19 (out_2[18], in_1[18]);
  not not_20 (out_2[19], in_1[19]);
  not not_21 (out_2[20], in_1[20]);
  not not_22 (out_2[21], in_1[21]);
  not not_23 (out_2[22], in_1[22]);
  not not_24 (out_2[23], in_1[23]);
  not not_25 (out_2[24], in_1[24]);
  not not_26 (out_2[25], in_1[25]);
  not not_27 (out_2[26], in_1[26]);
  not not_28 (out_2[27], in_1[27]);
  not not_29 (out_2[28], in_1[28]);
  not not_30 (out_2[29], in_1[29]);
  not not_31 (out_2[30], in_1[30]);
  not not_32 (out_2[31], in_1[31]);
  // Pins of 16 and 32 bits meet at in_1
  // Pins of 16 and 32 bits meet at out_2

  // Notes on the sheet:
  //   in_1: default 4
endmodule
