// Digital circuit 4bit_adder.dig as structural Verilog
module _4bit_adder (
  input  [3:0] A,
  input  [3:0] B,
  input  cin,
  output carry,
  output [3:0] sum
);

  wire full_adder_1_carry, full_adder_2_carry, full_adder_3_carry;

  full_adder full_adder_1 (.a(A[0]), .b(B[0]), .cin(cin), .sum(sum[0]), .carry(full_adder_1_carry));
  full_adder full_adder_2 (.a(A[1]), .b(B[1]), .cin(full_adder_1_carry), .sum(sum[1]), .carry(full_adder_2_carry));
  full_adder full_adder_3 (.a(A[2]), .b(B[2]), .cin(full_adder_2_carry), .sum(sum[2]), .carry(full_adder_3_carry));
  full_adder full_adder_4 (.a(A[3]), .b(B[3]), .cin(full_adder_3_carry), .sum(sum[3]), .carry(carry));

  // Notes on the sheet:
  //   A: default 4
endmodule
