// Digital circuit 4to16_decoder_enable.dig as structural Verilog
module _4to16_decoder_enable (
  input  [3:0] S,
  input  E,
  output out0,
  output out1,
  output out2,
  output out3,
  output out4,
  output out5,
  output out6,
  output out7,
  output out8,
  output out9,
  output out10,
  output out11,
  output out12,
  output out13,
  output out14,
  output out15
);

  wire decoder_1_out_0, decoder_1_out_1, decoder_1_out_2, decoder_1_out_3, decoder_1_out_4, decoder_1_out_5,
       decoder_1_out_6, decoder_1_out_7, decoder_1_out_8, decoder_1_out_9, decoder_1_out_10,
       decoder_1_out_11, decoder_1_out_12, decoder_1_out_13, decoder_1_out_14, decoder_1_out_15;

  Decoder #(.Selector_Bits(4)) decoder_1 (
    .sel(S), .out_0(decoder_1_out_0), .out_1(decoder_1_out_1), .out_2(decoder_1_out_2),
    .out_3(decoder_1_out_3), .out_4(decoder_1_out_4), .out_5(decoder_1_out_5), .out_6(decoder_1_out_6),
    .out_7(decoder_1_out_7), .out_8(decoder_1_out_8), .out_9(decoder_1_out_9), .out_10(decoder_1_out_10),
    .out_11(decoder_1_out_11), .out_12(decoder_1_out_12), .out_13(decoder_1_out_13),
    .out_14(decoder_1_out_14), .out_15(decoder_1_out_15));
  and and_1 (out0, decoder_1_out_0, E);
  and and_2 (out1, decoder_1_out_1, E);
  and and_3 (out2, decoder_1_out_2, E);
  and and_4 (out3, decoder_1_out_3, E);
  and and_5 (out4, decoder_1_out_4, E);
  and and_6 (out5, decoder_1_out_5, E);
  and and_7 (out6, decoder_1_out_6, E);
  and and_8 (out7, decoder_1_out_7, E);
  and and_9 (out8, decoder_1_out_8, E);
  and and_10 (out9, decoder_1_out_9, E);
  and and_11 (out10, decoder_1_out_10, E);
  and and_12 (out11, decoder_1_out_11, E);
  and and_13 (out12, decoder_1_out_12, E);
  and and_14 (out13, decoder_1_out_13, E);
  and and_15 (out14, decoder_1_out_14, E);
  and and_16 (out15, decoder_1_out_15, E);

  // Notes on the sheet:
  //   S: default 4
  //   E: default 1
endmodule
