// Digital circuit 4to1_1bit_mux.dig as structural Verilog
module _4to1_1bit_mux (
  input  A0,
  input  A1,
  input  A2,
  input  A3,
  input  [1:0] S,
  output Out
);

  wire _2to1_1bit_mux_1_out, _2to1_1bit_mux_2_out;

  _2to1_1bit_mux _2to1_1bit_mux_1 (.S(S[0]), .A(A2), .B(A3), .Out(_2to1_1bit_mux_1_out));
  _2to1_1bit_mux _2to1_1bit_mux_2 (.S(S[0]), .A(A0), .B(A1), .Out(_2to1_1bit_mux_2_out));
  _2to1_1bit_mux _2to1_1bit_mux_3 (.S(S[1]), .A(_2to1_1bit_mux_2_out), .B(_2to1_1bit_mux_1_out), .Out(Out));
endmodule
