// Digital circuit 8to1_1bit_mux.dig as structural Verilog
module _8to1_1bit_mux (
  input  A0,
  input  A1,
  input  A2,
  input  A3,
  input  [2:0] S,
  input  A4,
  input  A5,
  input  A6,
  input  A7,
  output [7:0] Out
);

  wire _4to1_1bit_mux_1_out, _4to1_1bit_mux_2_out;

  _4to1_1bit_mux _4to1_1bit_mux_1 (.A0(A0), .A1(A1), .A2(A2), .A3(A3), .S(S[1:0]), .Out(_4to1_1bit_mux_1_out));
  _4to1_1bit_mux _4to1_1bit_mux_2 (.A0(A4), .A1(A5), .A2(A6), .A3(A7), .S(S[1:0]), .Out(_4to1_1bit_mux_2_out));
  // _2to1_1bit_mux _2to1_1bit_mux_1: pin names not known; wires that end beside it: S[2], _4to1_1bit_mux_1_out, _4to1_1bit_mux_2_out, Out
endmodule
