// Digital circuit branch_24bit_sign_extended.dig as structural Verilog
module branch_24bit_sign_extended (
  input  [31:0] IW,
  output [31:0] Zero_ext
);


  assign Zero_ext = {{7{IW[23]}}, IW[22:0], 2'b00};
endmodule
