// Digital circuit branch_iw_splitter.dig as structural Verilog
module branch_iw_splitter (
  input  [31:0] iw,
  output [23:0] offset,
  output L_bit,
  output [2:0] _101,
  output [3:0] cond
);


  assign _101 = iw[27:25];
  assign cond = iw[31:28];
  assign L_bit = iw[24];
  assign offset = iw[23:0];
endmodule
