// Digital circuit bx_iw_splitter.dig as structural Verilog
module bx_iw_splitter (
  input  [31:0] iw,
  output [3:0] rn,
  output [23:0] bx_set_bits,
  output [3:0] cond
);


  assign bx_set_bits = iw[27:4];
  assign cond = iw[31:28];
  assign rn = iw[3:0];
endmodule
