// Digital circuit control_unit_3.dig as structural Verilog
module control_unit_3 (
  input  [31:0] iw,
  output RFW,
  output [1:0] EXT,
  output [1:0] ALUop,
  output BR,
  output ALU1src,
  output BL,
  output BX,
  output DataType,
  output conditional,
  output MW,
  output MR
);

  wire add_i, add_r, and_1_out, cmp_i, cmp_r, comparator_1_eq, comparator_2_eq, comparator_3_eq,
       comparator_4_eq, ldr_i, ldr_r, mov_i, mov_r, mul_r, or_1_out, or_2_out, or_3_out, or_4_out, or_5_out,
       or_6_out, or_7_out, sub_i, sub_r;

  // Probe on iw
  and and_1 (and_1_out, ~iw[27], iw[26]);  // And
  Comparator #(.Bits(4)) comparator_1 (.a(iw[24:21]), .b(4'b0100), .eq(comparator_1_eq));  // open: gt, lt
  Comparator #(.Bits(4)) comparator_2 (.a(iw[24:21]), .b(4'b0010), .eq(comparator_2_eq));  // open: gt, lt
  Comparator #(.Bits(4)) comparator_3 (.a(iw[24:21]), .b(4'b1101), .eq(comparator_3_eq));  // open: gt, lt
  Comparator #(.Bits(4)) comparator_4 (.a(iw[24:21]), .b(4'b1010), .eq(comparator_4_eq));  // open: gt, lt
  and and_2 (ldr_i, iw[20], and_1_out, ~iw[25]);  // And
  and and_3 (ldr_r, iw[20], and_1_out, iw[25]);
  and and_4 (MW, ~iw[20], and_1_out, ~iw[25]);  // And
  and and_5 (add_r, ~iw[27], ~iw[26], ~iw[25], comparator_1_eq);  // And
  and and_6 (add_i, ~iw[27], ~iw[26], iw[25], comparator_1_eq);  // And
  and and_7 (sub_i, ~iw[27], ~iw[26], iw[25], comparator_2_eq);  // And
  and and_8 (sub_r, ~iw[27], ~iw[26], ~iw[25], comparator_2_eq);  // And
  and and_9 (mov_i, ~iw[27], ~iw[26], iw[25], comparator_3_eq);  // And
  and and_10 (mov_r, ~iw[27], ~iw[26], ~iw[25], comparator_3_eq);  // And
  and and_11 (cmp_i, ~iw[27], ~iw[26], iw[25], comparator_4_eq);  // And
  and and_12 (cmp_r, ~iw[27], ~iw[26], ~iw[25], comparator_4_eq);  // And
  and and_13 (BR, iw[27], ~iw[26], iw[25]);  // And
  and and_14 (BL, BR, iw[24]);
  Comparator #(.Bits(24)) comparator_5 (.a(iw[27:4]), .b(24'h12fff1), .eq(BX));  // open: gt, lt
  or or_1 (or_1_out, add_r, add_i, sub_r, sub_i, ldr_r, ldr_i, mov_i, mov_r, BL, mul_r);
  or or_2 (or_2_out, mov_r, mov_i, sub_i, sub_r, cmp_r, cmp_i);
  or or_3 (or_3_out, mov_r, mov_i, mul_r);
  or or_4 (or_4_out, add_i, mov_i, sub_i, MW, ldr_i, BL, BR, cmp_i);
  or or_5 (or_5_out, ldr_r, ldr_i);
  or or_6 (or_6_out, BR, BL);
  or or_7 (or_7_out, cmp_i, BR, cmp_r);
  or or_8 (RFW, or_1_out, 1'b0);
  or or_9 (EXT[0], or_5_out, 1'b0);
  or or_10 (EXT[1], or_6_out, 1'b0);
  or or_11 (ALUop[0], or_2_out, 1'b0);
  or or_12 (ALUop[1], or_3_out, 1'b0);
  or or_13 (ALU1src, or_4_out, 1'b0);
  or or_14 (DataType, mul_r, 1'b0);
  or or_15 (conditional, or_7_out, 1'b0);
  Comparator #(.Bits(6)) comparator_6 (.a(iw[27:22]), .b({6{1'b0}}), .eq(mul_r));  // open: gt, lt
  or or_16 (MR, ldr_r, ldr_i);

  // Other names for the same wires on the sheet: b_offset[23:0] = iw[23:0]; imm[7:0] = iw[7:0];
  //   immoff[11:0] = iw[11:0]; rm[3:0] = iw[3:0]; rm_mul[3:0] = iw[3:0]; bxcode[23:0] = iw[27:4];
  //   opmul4[3:0] = iw[7:4]; rs_mul[3:0] = iw[11:8]; rd[3:0] = iw[15:12]; rn_mul[3:0] = iw[15:12];
  //   rd_mul[3:0] = iw[19:16]; rn[3:0] = iw[19:16]; l_sdt = iw[20]; s_dp = iw[20]; s_mul = iw[20]; a_mul = iw[21];
  //   opc[3:0] = iw[24:21]; w_sdt = iw[21]; b_sdt = iw[22]; opmul6[5:0] = iw[27:22]; u_sdt = iw[23]; l_b = iw[24];
  //   p_sdt = iw[24]; i_sdt = iw[25]; op0 = iw[25]; op0_i_dp = iw[25]; op1 = iw[26]; opmul2[1:0] = iw[27:26];
  //   op2 = iw[27]; cond[3:0] = iw[31:28]; mulcond[3:0] = iw[31:28]; sdtcond[3:0] = iw[31:28]; str_i = MW

  // Notes on the sheet:
  //   ldr(r)
  //   str(i)
  //   add(r)
  //   add(i)
  //   sub(i)
  //   sub(r)
  //   mov(i)
  //   mov(r)
  //   cmp(i)
  //   cmp(r)
  //   b
  //   bl
  //   ldr(i)
  //   all immediates
endmodule
