// Digital circuit control_unit_conditional.dig as structural Verilog
module control_unit_conditional (
  input  [31:0] iw,
  input  [3:0] NZCV,
  input  CLK,
  output RFW,
  output [1:0] EXT,
  output [1:0] ALUop,
  output ALU1src,
  output BR,
  output BL,
  output BX,
  output DataType,
  output MR,
  output MW
);

  wire AL_eq, and_1_out, and_2_out, and_3_out, and_4_out, and_6_out, C, control_unit_3_1_br,
       control_unit_3_1_conditional, EQ_eq, GT_eq, LE_eq, LT_eq, N, N___eq__V_2_eq, N___eq__V_eq,
       N__eq__eq__V_eq, NE_eq, or_1_out, or_2_out, V, Z;

  control_unit_3 control_unit_3_1 (
    .iw(iw), .RFW(RFW), .EXT(EXT), .ALUop(ALUop), .ALU1src(ALU1src), .DataType(DataType),
    .conditional(control_unit_3_1_conditional), .MW(MW), .MR(MR), .BR(control_unit_3_1_br), .BL(BL), .BX(BX));
  Register #(.Bits(4)) register_1 (.D(NZCV), .C(CLK), .en(control_unit_3_1_conditional), .Q({V, C, Z, N}));
  Comparator #(.Bits(4)) AL (.a(iw[31:28]), .b(4'b1110), .eq(AL_eq));  // open: gt, lt
  Comparator #(.Bits(4)) EQ (.a(iw[31:28]), .b(4'b0000), .eq(EQ_eq));  // open: gt, lt
  Comparator #(.Bits(4)) NE (.a(iw[31:28]), .b(4'b0001), .eq(NE_eq));  // open: gt, lt
  Comparator #(.Bits(4)) LT (.a(iw[31:28]), .b(4'b1011), .eq(LT_eq));  // open: gt, lt
  Comparator #(.Bits(4)) GT (.a(iw[31:28]), .b(4'b1100), .eq(GT_eq));  // open: gt, lt
  Comparator #(.Bits(4)) LE (.a(iw[31:28]), .b(4'b1101), .eq(LE_eq));  // open: gt, lt
  and and_1 (and_1_out, Z, EQ_eq);
  and and_2 (and_2_out, ~Z, NE_eq);  // And
  Comparator N___eq__V (.a(N), .b(V), .eq(N___eq__V_eq));  // open: gt, lt
  Comparator N__eq__eq__V (.a(N), .b(V), .eq(N__eq__eq__V_eq));  // open: gt, lt
  Comparator N___eq__V_2 (.a(N), .b(V), .eq(N___eq__V_2_eq));  // open: gt, lt
  and and_3 (and_3_out, LT_eq, ~N___eq__V_eq);  // And
  or or_1 (or_1_out, ~N___eq__V_2_eq, Z);  // Or
  and and_4 (and_4_out, GT_eq, ~Z, N__eq__eq__V_eq);  // And
  and and_5 (BR, control_unit_3_1_br, or_2_out);
  or or_2 (or_2_out, AL_eq, and_1_out, and_2_out, and_3_out, and_4_out, and_6_out);
  and and_6 (and_6_out, LE_eq, or_1_out);
endmodule
