// Digital circuit control_unit_tutorial.dig as structural Verilog
module control_unit_tutorial (
  input  [31:0] IW,
  output RFW,
  output ALU1src,
  output BR,
  output [1:0] EXT,
  output [1:0] ALUop
);

  wire and_1_out, and_3_out, and_4_out, comparator_1_eq, comparator_2_eq;

  Comparator #(.Bits(4)) comparator_1 (.a(IW[24:21]), .b(4'b0100), .eq(comparator_1_eq));  // open: gt, lt
  Comparator #(.Bits(4)) comparator_2 (.a(IW[24:21]), .b(4'b1101), .eq(comparator_2_eq));  // open: gt, lt
  and and_1 (and_1_out, ~IW[27], ~IW[26], ~IW[25], comparator_1_eq);  // And
  // And and_2 has open pins: In_1=IW[27], In_2=IW[26], In_3=open, In_4=open, out=open
  and and_3 (and_3_out, ~IW[27], ~IW[26], IW[25], comparator_2_eq);  // And
  and and_4 (and_4_out, IW[27], ~IW[26], IW[25]);  // And
  or or_1 (RFW, and_1_out, and_3_out);
  or or_2 (EXT[0], 1'b0, 1'b0);
  or or_3 (EXT[1], and_4_out, 1'b0);
  or or_4 (ALUop[0], and_3_out, 1'b0);
  or or_5 (ALUop[1], and_3_out, 1'b0);
  or or_6 (ALU1src, and_3_out, and_4_out);
  or or_7 (BR, and_4_out, 1'b0);

  // Other names for the same wires on the sheet: b_offset[23:0] = IW[23:0]; imm[7:0] = IW[7:0];
  //   immoff[11:0] = IW[11:0]; rm[3:0] = IW[3:0]; rm_mul[3:0] = IW[3:0]; opmul4[3:0] = IW[7:4];
  //   rs_mul[3:0] = IW[11:8]; rd[3:0] = IW[15:12]; rn_mul[3:0] = IW[15:12]; rd_mul[3:0] = IW[19:16];
  //   rn[3:0] = IW[19:16]; l_sdt = IW[20]; s_dp = IW[20]; s_mul = IW[20]; a_mul = IW[21]; opc[3:0] = IW[24:21];
  //   w_sdt = IW[21]; b_sdt = IW[22]; opmul6[4:0] = IW[27:23]; u_sdt = IW[23]; l_b = IW[24]; p_sdt = IW[24];
  //   i_dp = IW[25]; i_sdt = IW[25]; op0 = IW[25]; op1 = IW[26]; opmul2[1:0] = IW[27:26]; op2 = IW[27];
  //   cond[3:0] = IW[31:28]

  // Notes on the sheet:
  //   add(r)
  //   add(i)
endmodule
