// Digital circuit d_flipflop_clr.dig as structural Verilog
module d_flipflop_clr (
  input  D,
  input  CLR,
  input  CLK,
  output Q,
  output not_Q
);

  wire d_latch_clear_1_q, not_1_out;

  not not_1 (not_1_out, CLK);
  d_latch_clear d_latch_clear_1 (.D(D), .CLR(CLR), .CLK(not_1_out), .Q(d_latch_clear_1_q));  // open: not_Q
  d_latch_clear d_latch_clear_2 (.D(d_latch_clear_1_q), .CLR(CLR), .CLK(CLK), .Q(Q), .not_Q(not_Q));
endmodule
