// Digital circuit data_processing_8bit_zero_extended.dig as structural Verilog
module data_processing_8bit_zero_extended (
  input  [31:0] IW,
  output [31:0] Zero_ext
);


  assign Zero_ext = {{24{1'b0}}, IW[7:0]};
endmodule
