// Digital circuit data_processing_iw_splitter.dig as structural Verilog
module data_processing_iw_splitter (
  input  [31:0] iw,
  output [11:0] offset,
  output [3:0] rd,
  output [3:0] rn,
  output s,
  output [3:0] opcode,
  output op1,
  output [3:0] cond,
  output op2,
  output I_bit,
  output [7:0] shift,
  output [3:0] rm,
  output [7:0] imm
);

  wire [11:8] and_2_out;

  assign {shift, rm} = ~{12{iw[25]}} & iw[11:0];  // And and_1, 12 bits wide
  assign {and_2_out, imm} = {12{iw[25]}} & iw[11:0];  // And and_2, 12 bits wide

  assign cond = iw[31:28];
  assign I_bit = iw[25];
  assign offset = iw[11:0];
  assign op1 = iw[26];
  assign op2 = iw[27];
  assign opcode = iw[24:21];
  assign rd = iw[15:12];
  assign rn = iw[19:16];
  assign s = iw[20];
endmodule
