// Digital circuit instruction_memory_turnin.dig as structural Verilog
module instruction_memory_turnin (
  input  [31:0] A,
  input  [3:0] PN,
  output [31:0] D
);

  wire [31:0] fib_iter19_d, fib_iter_d, fib_rec19_d, fib_rec_d, find_max_d, quadratic_d, sum_array_d;

  ROM #(.AddrBits(5), .Bits(32)) sum_array (.A(A[6:2]), .sel(1'b1), .D(sum_array_d));
  ROM #(.AddrBits(5), .Bits(32)) quadratic (.A(A[6:2]), .sel(1'b1), .D(quadratic_d));
  ROM #(.AddrBits(5), .Bits(32)) fib_iter (.A(A[6:2]), .sel(1'b1), .D(fib_iter_d));
  ROM #(.AddrBits(5), .Bits(32)) fib_iter19 (.A(A[6:2]), .sel(1'b1), .D(fib_iter19_d));
  ROM #(.AddrBits(5), .Bits(32)) fib_rec (.A(A[6:2]), .sel(1'b1), .D(fib_rec_d));
  ROM #(.AddrBits(5), .Bits(32)) fib_rec19 (.A(A[6:2]), .sel(1'b1), .D(fib_rec19_d));
  ROM #(.AddrBits(5), .Bits(32)) find_max (.A(A[6:2]), .sel(1'b1), .D(find_max_d));
  Multiplexer #(.Selector_Bits(4), .Bits(32)) multiplexer_1 (
    .sel(PN), .in_0(sum_array_d), .in_1(quadratic_d), .in_2(fib_iter_d), .in_3(fib_iter19_d),
    .in_4(fib_rec_d), .in_5(fib_rec19_d), .in_6(find_max_d), .in_7({32{1'b0}}), .in_8({32{1'b0}}),
    .in_9({32{1'b0}}), .in_10({32{1'b0}}), .in_11({32{1'b0}}), .in_12({32{1'b0}}), .in_13({32{1'b0}}),
    .in_14({32{1'b0}}), .in_15({32{1'b0}}), .out(D));

  // Notes on the sheet:
  //   contents of sum_array (hex, n*v repeats v):
  //   e3a0d080,e24dd018,e3a00001,e58d0000,e3a00002,e58d0004,e3a00003,e58d0008,e3a00004,
  //   e58d000c,e3a00005,e58d0010,e3a00006,e58d0014,e1a0000d,e3a01006,eb000000,eafffffe,
  //   e3a02000,e3a03000,e1520001,a000004,e590c000,e083300c,e2822001,e2800004,eafffff8,e1a00003,
  //   e12fff1e
  //   contents of quadratic (hex, n*v repeats v):
  //   e3a00002,e3a01001,e3a02002,e3a03003,eb000000,eafffffe,e3a0c000,e00c0092,e08c3003,
  //   e1a0c000,e00c0c90,e000019c,e0830000,e12fff1e
  //   contents of fib_iter (hex, n*v repeats v):
  //   e3a0000a,eb000000,eafffffe,e3a01000,e3a02000,e3a03000,e3a0c001,e3500000,a000007,e2833001,
  //   e15c0000,a000004,e1a01002,e1a02003,e0813002,e28cc001,eafffff8,e1a00003,e12fff1e
  //   contents of fib_iter19 (hex, n*v repeats v):
  //   e3a00013,eb000000,eafffffe,e3a01000,e3a02000,e3a03000,e3a0c001,e3500000,a000007,e2833001,
  //   e15c0000,a000004,e1a01002,e1a02003,e0813002,e28cc001,eafffff8,e1a00003,e12fff1e
  //   contents of fib_rec (hex, n*v repeats v):
  //   e3a0000a,eb000000,eafffffe,e3a01000,e3a02000,e3a03000,e3a0c001,e3500000,a000007,e2833001,
  //   e15c0000,a000004,e1a01002,e1a02003,e0813002,e28cc001,eafffff8,e1a00003,e12fff1e
  //   contents of fib_rec19 (hex, n*v repeats v):
  //   e3a00013,eb000000,eafffffe,e24dd010,e3500000,a000012,e3500001,1a000001,e3a01001,ea00000b,
  //   e58de000,e58d0004,e2400001,ebfffffe,e1a01000,e58d1008,e59d0004,e2400002,ebffffef,
  //   e59d1008,e0801001,e59de000,e1a00001,e28dd010,e12fff1e,e3a01000,eafffffa
  //   contents of find_max (hex, n*v repeats v):
  //   e3a0d080,e24dd018,e3a00001,e58d0000,e3a00002,e58d0004,e3a00003,e58d0008,e3a00004,
  //   e58d000c,e3a00005,e58d0010,e1a0000d,e3a01005,eb000000,eafffffe,e3a02000,e5903000,
  //   e1520001,a000009,e590c000,e15c0003,ba000003,e1a0300c,e2822001,e2800004,eafffff6,e2822001,
  //   e2800004,eafffff3,e1a00003,e12fff1e
endmodule
