// Digital circuit instruction_word_split.dig as structural Verilog
module instruction_word_split (
  input  [31:0] word,
  output [31:0] val_rtshft
);


  assign val_rtshft = {2'b00, word[31:2]};
endmodule
