// Digital circuit memory_12bit_sign_extended.dig as structural Verilog
module memory_12bit_sign_extended (
  input  [31:0] IW,
  output [31:0] Zero_ext
);


  assign Zero_ext = {{20{1'b0}}, IW[11:0]};
endmodule
