// Digital circuit multiply_iw_splitter.dig as structural Verilog
module multiply_iw_splitter (
  input  [31:0] iw,
  output [3:0] rm,
  output [3:0] _1001,
  output [3:0] rs,
  output [3:0] rn,
  output [3:0] rd,
  output S_bit,
  output A_bit,
  output [5:0] _000000,
  output [3:0] cond
);


  assign _000000 = iw[27:22];
  assign _1001 = iw[7:4];
  assign A_bit = iw[21];
  assign cond = iw[31:28];
  assign rd = iw[19:16];
  assign rm = iw[3:0];
  assign rn = iw[15:12];
  assign rs = iw[11:8];
  assign S_bit = iw[20];
endmodule
