// Digital circuit processor_ext_unit.dig as structural Verilog
module processor_ext_unit (
  input  [31:0] IW,
  input  [1:0] S,
  output [31:0] extended
);

  wire [31:0] branch_24bit_sign_extended_1_zero_ext, data_processing_8bit_zero_extended_1_zero_ext,
       memory_12bit_sign_extended_1_zero_ext;

  data_processing_8bit_zero_extended data_processing_8bit_zero_extended_1 (
    .IW(IW), .Zero_ext(data_processing_8bit_zero_extended_1_zero_ext));
  memory_12bit_sign_extended memory_12bit_sign_extended_1 (.IW(IW), .Zero_ext(memory_12bit_sign_extended_1_zero_ext));
  branch_24bit_sign_extended branch_24bit_sign_extended_1 (.IW(IW), .Zero_ext(branch_24bit_sign_extended_1_zero_ext));
  Multiplexer #(.Selector_Bits(2), .Bits(32)) multiplexer_1 (
    .sel(S), .in_0(data_processing_8bit_zero_extended_1_zero_ext),
    .in_1(memory_12bit_sign_extended_1_zero_ext), .in_2(branch_24bit_sign_extended_1_zero_ext),
    .in_3({32{1'b0}}), .out(extended));
endmodule
