// Digital circuit project_first_a_code.dig as structural Verilog
module project_first_a_code (
  input  clk
);

  wire a_mul, ALU1src, and_1_out, BR, C, comparator_1_eq, dipswitch_1_out, i_dp, N, RFW, V, Z;
  wire [1:0] ALUop, EXT;
  wire [3:0] cond, multiplexer_2_out;
  wire [23:0] b_offset;
  wire [27:24] iw;
  wire [31:0] add_1_s, add_2_s, alu_1_r, multiplexer_3_out, pc_in, pc_out, processor_ext_unit_1_extended, r0,
       r1, r2, r3, r4, r5, r6, r7, r8, r9, r10, r11, r12, r13, r14, r15, register_file_1_rd0,
       register_file_1_rd1;

  // Probe on {cond, iw[27:26], i_dp, iw[24], b_offset[23:22], a_mul, b_offset[20:0]}
  and and_1 (and_1_out, clk, dipswitch_1_out);
  DipSwitch dipswitch_1 (.out(dipswitch_1_out));
  Multiplexer #(.Bits(32)) multiplexer_1 (.sel(BR), .in_0(add_1_s), .in_1(alu_1_r), .out(pc_in));
  // Probe on pc_in
  Register #(.Bits(32), .isProgramCounter("true")) PC (.D(pc_in), .C(and_1_out), .en(1'b1), .Q(pc_out));
  // Probe on pc_in
  // control_unit_2 control_unit_2_1: pin names not known; wires that end beside it: {cond, iw[27:26], i_dp, iw[24], b_offset[23:22], a_mul, b_offset[20:0]}, RFW, EXT, ALUop, ALU1src, BR
  // Probe on pc_out
  // Probe on pc_out
  Add #(.Bits(32)) add_1 (.a(pc_out), .b(32'h4), .c_i(1'b0), .s(add_1_s));  // open: c_o
  // Probe on r0
  // Probe on r1
  // Probe on r2
  // Probe on r3
  // Probe on b_offset[19:16]
  // Probe on b_offset[15:12]
  // Probe on b_offset[19:16]
  ROM #(.AddrBits(5), .Bits(32)) rom_1 (
    .A(pc_out[6:2]), .sel(1'b1), .D({cond, iw[27:26], i_dp, iw[24], b_offset[23:22], a_mul, b_offset[20:0]}));
  Add #(.Bits(32)) add_2 (.a(add_1_s), .b(32'h4), .c_i(1'b0), .s(add_2_s));  // open: c_o
  // Probe on r4
  // Probe on r5
  // Probe on r6
  // Probe on r7
  // Probe on b_offset[3:0]
  // Probe on b_offset[3:0]
  // Probe on b_offset[3:0]
  // Probe on {cond, iw[27:26], i_dp, iw[24], b_offset[23:22], a_mul, b_offset[20:0]}
  // Probe on b_offset[15:12]
  // Probe on b_offset[19:16]
  // Probe on b_offset[15:12]
  // Probe on r8
  // Probe on r9
  // Probe on r10
  // Probe on r11
  // Probe on b_offset[7:0]
  // Probe on b_offset[11:8]
  // Probe on b_offset[11:0]
  Multiplexer #(.Bits(4)) multiplexer_2 (.sel(BR), .in_0(b_offset[19:16]), .in_1(4'b1111), .out(multiplexer_2_out));
  // Probe on b_offset[3:0]
  // Probe on b_offset[19:16]
  // Probe on b_offset[15:12]
  // Probe on r12
  // Probe on r13
  // Probe on r14
  // Probe on r15
  // Probe on alu_1_r
  register_file register_file_1 (
    .ReadReg0(multiplexer_2_out), .ReadReg1(b_offset[3:0]), .WriteData(alu_1_r), .WriteEn(RFW),
    .WriteReg(b_offset[15:12]), .PC(add_2_s), .CLK(and_1_out), .RD0(register_file_1_rd0),
    .RD1(register_file_1_rd1), .r0(r0), .r1(r1), .r2(r2), .r3(r3), .r4(r4), .r5(r5), .r6(r6), .r7(r7),
    .r8(r8), .r9(r9), .r10(r10), .r11(r11), .r12(r12), .r13(r13), .r14(r14), .r15(r15));
  // Probe on cond
  // Probe on cond
  // Probe on cond
  // Probe on cond
  // Probe on N
  // Probe on Z
  // Probe on C
  // Probe on V
  // Probe on iw[27:26]
  // Probe on {iw[27:26], i_dp, iw[24], b_offset[23]}
  // Probe on iw[27:26]
  // Probe on {iw[27:26], i_dp}
  Comparator #(.Bits(32)) comparator_1 (.a(pc_in), .b(pc_out), .eq(comparator_1_eq));  // open: gt, lt
  // Probe on pc_in
  // Probe on pc_out
  // Probe on EXT
  // Probe on {iw[24], b_offset[23:22], a_mul}
  // Probe on b_offset[7:4]
  // Probe on i_dp
  // Probe on iw[24]
  ALU alu_1 (
    .A(register_file_1_rd0), .B(multiplexer_3_out), .ALUOp(ALUop), .R(alu_1_r), .N(N), .Z(Z), .C(C), .V(V));  // open: NZCV
  Multiplexer #(.Bits(32)) multiplexer_3 (
    .sel(ALU1src), .in_0(register_file_1_rd1), .in_1(processor_ext_unit_1_extended), .out(multiplexer_3_out));
  processor_ext_unit processor_ext_unit_1 (
    .IW({cond, iw[27:26], i_dp, iw[24], b_offset[23:22], a_mul, b_offset[20:0]}), .S(EXT),
    .extended(processor_ext_unit_1_extended));
  LED led_1 (.in(comparator_1_eq));
  // Probe on i_dp
  // Probe on a_mul
  // Probe on iw[24]
  // Probe on {b_offset[23:22], a_mul, b_offset[20:0]}
  // Probe on processor_ext_unit_1_extended
  // Probe on b_offset[20]
  // Probe on b_offset[20]
  // Probe on b_offset[23]
  // Probe on alu_1_r
  // Probe on b_offset[22]
  // Probe on a_mul
  // Probe on b_offset[20]

  // Other names for the same wires on the sheet: imm[7:0] = b_offset[7:0]; immoff[11:0] = b_offset[11:0];
  //   iw (some bits) = {cond, i_dp, b_offset[23:22], a_mul, b_offset[20:0]}; rm[3:0] = b_offset[3:0];
  //   rm_mul[3:0] = b_offset[3:0]; opmul4[3:0] = b_offset[7:4]; rs_mul[3:0] = b_offset[11:8];
  //   rd[3:0] = b_offset[15:12]; rn_mul[3:0] = b_offset[15:12]; rd_mul[3:0] = b_offset[19:16];
  //   rn[3:0] = b_offset[19:16]; l_sdt = b_offset[20]; s_dp = b_offset[20]; s_mul = b_offset[20];
  //   b_offset[21] = a_mul; opc[3:0] = {iw[24], b_offset[23:22], a_mul}; w_sdt = a_mul; b_sdt = b_offset[22];
  //   opmul6[4:0] = {iw[27:26], i_dp, iw[24], b_offset[23]}; u_sdt = b_offset[23]; l_b = iw[24]; p_sdt = iw[24];
  //   i_sdt = i_dp; opb3[2:0] = {iw[27:26], i_dp}; op2[1:0] = iw[27:26]; opmul2[1:0] = iw[27:26]

  // Notes on the sheet:
  //   DP
  //   MUL
  //   SDT
  //   B
  //   contents of rom_1 (hex, n*v repeats v):
  //   e3a00001,e3a01002,e0802001,eaffffffe
endmodule
