// Digital circuit project_first_main_added_branches.dig as structural Verilog
module project_first_main_added_branches (
  input  clk
);

  wire a_mul, ALU1src, and_1_out, BL, BR, BX, C, comparator_1_eq, DataType, dipswitch_1_out, MR, MW, N, RFW,
       V, Z;
  wire [1:0] ALUop, EXT;
  wire [3:0] cond, multiplexer_3_out, multiplexer_4_out, multiplexer_5_out, multiplexer_6_out,
       multiplexer_8_out, NZCV;
  wire [23:0] b_offset;
  wire [23:20] bxcode;
  wire [31:0] add_1_s, add_2_s, alu_1_p2, alu_1_p4, ldr_d, multiplexer_1_out, multiplexer_7_out,
       multiplexer_9_out, pc_in, pc_out, processor_ext_unit_1_extended, r0, r1, r2, r3, r4, r5, r6, r7, r8,
       r9, r10, r11, r12, r13, r14, r15, register_file_1_rd0, register_file_1_rd1;

  Multiplexer #(.Bits(32)) multiplexer_1 (.sel(BR), .in_0(add_1_s), .in_1(alu_1_p4), .out(multiplexer_1_out));
  and and_1 (and_1_out, clk, dipswitch_1_out);
  DipSwitch dipswitch_1 (.out(dipswitch_1_out));
  // Probe on {cond, bxcode, b_offset[23:22], a_mul, b_offset[20:0]}
  Multiplexer #(.Bits(32)) multiplexer_2 (.sel(BX), .in_0(multiplexer_1_out), .in_1(register_file_1_rd1), .out(pc_in));
  Register #(.Bits(32), .isProgramCounter("true")) PC (.D(pc_in), .C(and_1_out), .en(1'b1), .Q(pc_out));
  control_unit_conditional control_unit_conditional_1 (
    .iw({cond, bxcode, b_offset[23:22], a_mul, b_offset[20:0]}), .NZCV(NZCV), .CLK(and_1_out), .RFW(RFW),
    .EXT(EXT), .ALUop(ALUop), .ALU1src(ALU1src), .BR(BR), .BL(BL), .BX(BX), .DataType(DataType), .MR(MR),
    .MW(MW));
  Add #(.Bits(32)) add_1 (.a(pc_out), .b(32'h4), .c_i(1'b0), .s(add_1_s));  // open: c_o
  instruction_memory_turnin instruction_memory_turnin_1 (
    .A(pc_out), .PN(4'b0001), .D({cond, bxcode, b_offset[23:22], a_mul, b_offset[20:0]}));
  // Probe on r0
  // Probe on r1
  // Probe on r2
  // Probe on r3
  // Probe on b_offset[19:16]
  // Probe on b_offset[15:12]
  // Probe on b_offset[19:16]
  // Probe on {bxcode, b_offset[23:22], a_mul, b_offset[20:4]}
  Multiplexer #(.Bits(4)) multiplexer_3 (
    .sel(DataType), .in_0(b_offset[19:16]), .in_1(b_offset[11:8]), .out(multiplexer_3_out));
  Multiplexer #(.Bits(4)) multiplexer_4 (
    .sel(DataType), .in_0(b_offset[15:12]), .in_1(b_offset[19:16]), .out(multiplexer_4_out));
  Add #(.Bits(32)) add_2 (.a(add_1_s), .b(32'h4), .c_i(1'b0), .s(add_2_s));  // open: c_o
  // Probe on r4
  // Probe on r5
  // Probe on r6
  // Probe on r7
  // Probe on b_offset[3:0]
  // Probe on b_offset[3:0]
  // Probe on b_offset[3:0]
  // Probe on b_offset[15:12]
  // Probe on b_offset[19:16]
  // Probe on b_offset[15:12]
  Multiplexer #(.Bits(4)) multiplexer_5 (
    .sel(MW), .in_0(b_offset[3:0]), .in_1(b_offset[15:12]), .out(multiplexer_5_out));
  // Probe on r8
  // Probe on r9
  // Probe on r10
  // Probe on r11
  Multiplexer #(.Bits(4)) multiplexer_6 (.sel(BL), .in_0(multiplexer_4_out), .in_1(4'b1110), .out(multiplexer_6_out));
  Multiplexer #(.Bits(32)) multiplexer_7 (.sel(BL), .in_0(alu_1_p4), .in_1(add_1_s), .out(multiplexer_7_out));
  // Probe on b_offset[7:0]
  // Probe on b_offset[11:8]
  // Probe on b_offset[11:0]
  Multiplexer #(.Bits(4)) multiplexer_8 (.sel(BR), .in_0(multiplexer_3_out), .in_1(4'b1111), .out(multiplexer_8_out));
  // Probe on r12
  // Probe on r13
  // Probe on r14
  // Probe on r15
  // Probe on cond
  // Probe on cond
  // Probe on cond
  // Probe on cond
  Multiplexer #(.Bits(32)) multiplexer_9 (.sel(MR), .in_0(multiplexer_7_out), .in_1(ldr_d), .out(multiplexer_9_out));
  // Probe on N
  // Probe on Z
  // Probe on C
  // Probe on V
  register_file register_file_1 (
    .ReadReg0(multiplexer_8_out), .ReadReg1(multiplexer_5_out), .WriteData(multiplexer_9_out), .WriteEn(RFW),
    .WriteReg(multiplexer_6_out), .PC(add_2_s), .CLK(and_1_out), .RD0(register_file_1_rd0),
    .RD1(register_file_1_rd1), .r0(r0), .r1(r1), .r2(r2), .r3(r3), .r4(r4), .r5(r5), .r6(r6), .r7(r7),
    .r8(r8), .r9(r9), .r10(r10), .r11(r11), .r12(r12), .r13(r13), .r14(r14), .r15(r15));
  // Probe on bxcode[23:22]
  // Probe on {bxcode, b_offset[23]}
  // Probe on bxcode[23:22]
  // Probe on bxcode[23:21]
  Comparator #(.Bits(32)) comparator_1 (.a(pc_in), .b(pc_out), .eq(comparator_1_eq));  // open: gt, lt
  // Probe on pc_in
  // Probe on pc_out
  // Probe on EXT
  // Probe on {bxcode[20], b_offset[23:22], a_mul}
  // Probe on b_offset[7:4]
  // Probe on bxcode[21]
  // Probe on bxcode[20]
  LED led_1 (.in(comparator_1_eq));
  // Probe on bxcode[21]
  // Probe on a_mul
  // Probe on bxcode[20]
  // Probe on {b_offset[23:22], a_mul, b_offset[20:0]}
  // Probe on b_offset[20]
  // Probe on b_offset[20]
  // Probe on b_offset[23]
  // alu alu_1: pin names not known; wires that end beside it: register_file_1_rd0, alu_1_p2, ALUop, alu_1_p4, NZCV, N, Z, C, V
  Multiplexer #(.Bits(32)) multiplexer_10 (
    .sel(ALU1src), .in_0(register_file_1_rd1), .in_1(processor_ext_unit_1_extended), .out(alu_1_p2));
  processor_ext_unit processor_ext_unit_1 (
    .IW({cond, bxcode, b_offset[23:22], a_mul, b_offset[20:0]}), .S(EXT),
    .extended(processor_ext_unit_1_extended));
  // Probe on b_offset[22]
  // Probe on a_mul
  // Probe on b_offset[20]
  RAMDualPort #(.AddrBits(9), .Bits(32)) ldr (
    .A(alu_1_p4[10:2]), .Din(register_file_1_rd1), .str(MW), .C(clk), .ld(MR), .D(ldr_d));

  // Other names for the same wires on the sheet: imm[7:0] = b_offset[7:0]; immoff[11:0] = b_offset[11:0];
  //   iw[31:0] = {cond, bxcode, b_offset[23:22], a_mul, b_offset[20:0]}; rm[3:0] = b_offset[3:0];
  //   rm_mul[3:0] = b_offset[3:0]; bxcode[19:0] = {b_offset[23:22], a_mul, b_offset[20:4]};
  //   opmul4[3:0] = b_offset[7:4]; rs_mul[3:0] = b_offset[11:8]; rd[3:0] = b_offset[15:12];
  //   rn_mul[3:0] = b_offset[15:12]; rd_mul[3:0] = b_offset[19:16]; rn[3:0] = b_offset[19:16]; l_sdt = b_offset[20];
  //   s_dp = b_offset[20]; s_mul = b_offset[20]; b_offset[21] = a_mul;
  //   opc[3:0] = {bxcode[20], b_offset[23:22], a_mul}; w_sdt = a_mul; b_sdt = b_offset[22];
  //   opmul6[4:0] = {bxcode, b_offset[23]}; u_sdt = b_offset[23]; l_b = bxcode[20]; p_sdt = bxcode[20];
  //   i_dp = bxcode[21]; i_sdt = bxcode[21]; opb3[2:0] = bxcode[23:21]; op2[1:0] = bxcode[23:22];
  //   opmul2[1:0] = bxcode[23:22]

  // Notes on the sheet:
  //   clk: Hz: 2147483647
  //   DP
  //   MUL
  //   SDT
  //   B
  //   rd
  //   rn
  //   sp
  //   lr
  //   pc + 8
  //   pc
endmodule
