// Digital circuit register_file.dig as structural Verilog
module register_file (
  input  [3:0] ReadReg0,
  input  [3:0] ReadReg1,
  input  [31:0] WriteData,
  input  WriteEn,
  input  [3:0] WriteReg,
  input  [31:0] PC,
  input  CLK,
  output [31:0] RD0,
  output [31:0] RD1,
  output [31:0] r0,
  output [31:0] r1,
  output [31:0] r2,
  output [31:0] r3,
  output [31:0] r4,
  output [31:0] r5,
  output [31:0] r6,
  output [31:0] r7,
  output [31:0] r8,
  output [31:0] r9,
  output [31:0] r10,
  output [31:0] r11,
  output [31:0] r12,
  output [31:0] r13,
  output [31:0] r14,
  output [31:0] r15
);

  wire _4to16_decoder_enable_1_out0, _4to16_decoder_enable_1_out1, _4to16_decoder_enable_1_out2,
       _4to16_decoder_enable_1_out3, _4to16_decoder_enable_1_out4, _4to16_decoder_enable_1_out5,
       _4to16_decoder_enable_1_out6, _4to16_decoder_enable_1_out7, _4to16_decoder_enable_1_out8,
       _4to16_decoder_enable_1_out9, _4to16_decoder_enable_1_out10, _4to16_decoder_enable_1_out11,
       _4to16_decoder_enable_1_out12, _4to16_decoder_enable_1_out13, _4to16_decoder_enable_1_out14;

  _4to16_decoder_enable _4to16_decoder_enable_1 (
    .S(WriteReg), .E(WriteEn), .out0(_4to16_decoder_enable_1_out0), .out1(_4to16_decoder_enable_1_out1),
    .out2(_4to16_decoder_enable_1_out2), .out3(_4to16_decoder_enable_1_out3),
    .out4(_4to16_decoder_enable_1_out4), .out5(_4to16_decoder_enable_1_out5),
    .out6(_4to16_decoder_enable_1_out6), .out7(_4to16_decoder_enable_1_out7),
    .out8(_4to16_decoder_enable_1_out8), .out9(_4to16_decoder_enable_1_out9),
    .out10(_4to16_decoder_enable_1_out10), .out11(_4to16_decoder_enable_1_out11),
    .out12(_4to16_decoder_enable_1_out12), .out13(_4to16_decoder_enable_1_out13),
    .out14(_4to16_decoder_enable_1_out14));  // open: out15
  Register #(.Bits(32)) register_1 (.D(WriteData), .C(CLK), .en(_4to16_decoder_enable_1_out0), .Q(r0));
  Register #(.Bits(32)) register_2 (.D(WriteData), .C(CLK), .en(_4to16_decoder_enable_1_out1), .Q(r1));
  Register #(.Bits(32)) register_3 (.D(WriteData), .C(CLK), .en(_4to16_decoder_enable_1_out2), .Q(r2));
  Register #(.Bits(32)) register_4 (.D(WriteData), .C(CLK), .en(_4to16_decoder_enable_1_out3), .Q(r3));
  Register #(.Bits(32)) register_5 (.D(WriteData), .C(CLK), .en(_4to16_decoder_enable_1_out4), .Q(r4));
  Register #(.Bits(32)) register_6 (.D(WriteData), .C(CLK), .en(_4to16_decoder_enable_1_out5), .Q(r5));
  Register #(.Bits(32)) register_7 (.D(WriteData), .C(CLK), .en(_4to16_decoder_enable_1_out6), .Q(r6));
  Register #(.Bits(32)) register_8 (.D(WriteData), .C(CLK), .en(_4to16_decoder_enable_1_out7), .Q(r7));
  Register #(.Bits(32)) register_9 (.D(WriteData), .C(CLK), .en(_4to16_decoder_enable_1_out8), .Q(r8));
  Register #(.Bits(32)) register_10 (.D(WriteData), .C(CLK), .en(_4to16_decoder_enable_1_out9), .Q(r9));
  Register #(.Bits(32)) register_11 (.D(WriteData), .C(CLK), .en(_4to16_decoder_enable_1_out10), .Q(r10));
  Register #(.Bits(32)) register_12 (.D(WriteData), .C(CLK), .en(_4to16_decoder_enable_1_out11), .Q(r11));
  Register #(.Bits(32)) register_13 (.D(WriteData), .C(CLK), .en(_4to16_decoder_enable_1_out12), .Q(r12));
  Register #(.Bits(32)) register_14 (.D(WriteData), .C(CLK), .en(_4to16_decoder_enable_1_out13), .Q(r13));
  Register #(.Bits(32)) register_15 (.D(WriteData), .C(CLK), .en(_4to16_decoder_enable_1_out14), .Q(r14));
  Multiplexer #(.Selector_Bits(4), .Bits(32)) multiplexer_1 (
    .sel(ReadReg1), .in_0(r0), .in_1(r1), .in_2(r2), .in_3(r3), .in_4(r4), .in_5(r5), .in_6(r6), .in_7(r7),
    .in_8(r8), .in_9(r9), .in_10(r10), .in_11(r11), .in_12(r12), .in_13(r13), .in_14(r14), .in_15(PC),
    .out(RD1));
  Multiplexer #(.Selector_Bits(4), .Bits(32)) multiplexer_2 (
    .sel(ReadReg0), .in_0(r0), .in_1(r1), .in_2(r2), .in_3(r3), .in_4(r4), .in_5(r5), .in_6(r6), .in_7(r7),
    .in_8(r8), .in_9(r9), .in_10(r10), .in_11(r11), .in_12(r12), .in_13(r13), .in_14(r14), .in_15(PC),
    .out(RD0));

  assign r15 = PC;
endmodule
