// Digital circuit right_shift_2bits.dig as structural Verilog
module right_shift_2bits (
  input  [31:0] val,
  output [31:0] val_rtshft
);


  assign val_rtshft = {{3{val[31]}}, val[30:2]};
endmodule
