// Digital circuit single_data_transfer_iw_splitter.dig as structural Verilog
module single_data_transfer_iw_splitter (
  input  [31:0] iw,
  output [11:0] offset,
  output [3:0] rd,
  output [3:0] rn,
  output L_bit,
  output W_bit,
  output B_bit,
  output U_bit,
  output P_bit,
  output I_bit,
  output [1:0] _01_bits,
  output [3:0] cond,
  output [7:0] shift,
  output [3:0] rm,
  output [11:0] imm
);

  assign imm = ~{12{iw[25]}} & iw[11:0];  // And and_1, 12 bits wide
  assign {shift, rm} = {12{iw[25]}} & iw[11:0];  // And and_2, 12 bits wide

  assign _01_bits = iw[27:26];
  assign B_bit = iw[22];
  assign cond = iw[31:28];
  assign I_bit = iw[25];
  assign L_bit = iw[20];
  assign offset = iw[11:0];
  assign P_bit = iw[24];
  assign rd = iw[15:12];
  assign rn = iw[19:16];
  assign U_bit = iw[23];
  assign W_bit = iw[21];
endmodule
